# Fritzing sketch hexbotling_client_v0_4 (saved by Fritzing 0.9.4)
circuit board: 6.42483cm x 5.92033cm
breadboards: 4

parts:
  Cli = female pin header, 6 pins [form="♀ (female)"]
  3208 = SO16 [chip_label=SOIC-16 part_number="579-MCP3208CISL " package=SO]
  R1 = Resistor [tolerance=±5% resistance=470 package=THT]
  LED1 = LED - 3mm [color="Green (565nm)" package="3 mm [THT]"]
  S1 = SPST Switch [package=switch-spdt]
  NP = female pin header, 3 pins [form="♀ (female)"]
  LiPo_Battery_1100_mAh1 = Lithium Ion Polymer Battery 3.7v 350mAh [part_number=2750]
  Analog_In_c1 = female pin header, 8 pins [form="♀ (female)"]
  Analog_In_b1 = female pin header, 8 pins [form="♀ (female)"]
  Analog_In1 = female pin header, 8 pins [form="♀ (female)"]
  C4 = Tantalum Capacitor [capacitance=1μF package="100 mil [THT, tantalum]"]
  R2 = Resistor [tolerance=±5% resistance=680 package=THT]
  R3 = Resistor [tolerance=±5% resistance=8.2k package=THT]
  R4 = Resistor [tolerance=±5% resistance=8.2k package=THT]
  DIO_b1 = female pin header, 4 pins [form="♀ (female)"]
  DIO_c1 = female pin header, 4 pins [form="♀ (female)"]
  0-DIO-3 = female pin header, 4 pins [form="♀ (female)"]
  I2C2 = Header 4 [package=1x04-1mm-ra]
  I2C1 = Header 4 [package=1x04-1mm-ra]
  COM2 = female pin header, 8 pins [form="♀ (female)"]
  huzzah32 = Adafruit HUZZAH32 ESP32 Feather [part_number="Adafruit #3405"]
  J3 = male pin header, 3 pins [form="♂ (male)"]
  J2 = rounded female pin header, 4 pins [form="♀ (female rounded)"]
  J4 = male pin header, 2 pins [form="♂ (male)"]
  D1 = Rectifier Diode [part_number=1N4002 breakdown_voltage=3.6V package="300 mil [THT]"]
  COM2_2 = male pin header, 4 pins [form="♂ (male)"]
  DIO_b2 = male pin header, 4 pins [form="♂ (male)"]

nets:
  N1: Cli.pin1, huzzah32.IO17
  N2: Cli.pin2, huzzah32.IO16
  N3: Cli.pin4, huzzah32.IO32_A7
  N4: Cli.pin5, 3208.9, 3208.14, LED1.cathode, NP.pin1, LiPo_Battery_1100_mAh1.negative, Analog_In_b1.pin1, Analog_In_b1.pin2, Analog_In_b1.pin3, Analog_In_b1.pin4, Analog_In_b1.pin5, Analog_In_b1.pin6, Analog_In_b1.pin7, Analog_In_b1.pin8, C4.-, DIO_c1.pin1, DIO_c1.pin2, DIO_c1.pin3, DIO_c1.pin4, I2C2.1, I2C1.1, COM2.pin1, COM2.pin6, huzzah32.GND, J2.pin2, COM2_2.pin4, DIO_b2.pin4
  N5: 3208.1, Analog_In1.pin1
  N6: 3208.2, Analog_In1.pin2
  N7: 3208.3, Analog_In1.pin3
  N8: 3208.4, Analog_In1.pin4
  N9: 3208.5, Analog_In1.pin5
  N10: 3208.6, Analog_In1.pin6
  N11: 3208.7, Analog_In1.pin7
  N12: 3208.8, Analog_In1.pin8
  N13: 3208.10, huzzah32.IO33_A9
  N14: 3208.11, huzzah32.MOSI
  N15: 3208.12, huzzah32.MISO
  N16: 3208.13, huzzah32.SCK
  N17: 3208.15, 3208.16, NP.pin2, Analog_In_c1.pin1, Analog_In_c1.pin2, Analog_In_c1.pin3, Analog_In_c1.pin4, Analog_In_c1.pin5, Analog_In_c1.pin6, Analog_In_c1.pin7, Analog_In_c1.pin8, C4.+, DIO_b1.pin1, DIO_b1.pin2, DIO_b1.pin3, DIO_b1.pin4, COM2.pin2, J2.pin1, J4.pin1, COM2_2.pin3
  N18: R1.Pin_0, 0-DIO-3.pin4, huzzah32.A4_IO36
  N19: R1.Pin_1, LED1.anode
  N20: S1.P, huzzah32.VBAT
  N21: S1.S, LiPo_Battery_1100_mAh1.positive
  N22: NP.pin3, R2.Pin_0
  N23: R2.Pin_1, huzzah32.IO15_A8
  N24: R3.Pin_0, R4.Pin_0, I2C2.2, I2C1.2, J3.pin2, DIO_b2.pin3
  N25: R3.Pin_1, I2C2.3, I2C1.3, huzzah32.SDA, DIO_b2.pin1
  N26: R4.Pin_1, I2C2.4, I2C1.4, huzzah32.SCL, DIO_b2.pin2
  N27: 0-DIO-3.pin1, huzzah32.A0_DAC2
  N28: 0-DIO-3.pin2, huzzah32.A1_DAC1
  N29: 0-DIO-3.pin3, huzzah32.IO27_A10
  N30: COM2.pin7, huzzah32.IO14_A6, COM2_2.pin2
  N31: COM2.pin8, huzzah32.A5_IO4, COM2_2.pin1
  N32: huzzah32.IO21, J3.pin1
  N33: huzzah32.3.3V, J3.pin3
  N34: huzzah32.VBUS, D1.cathode
  N35: J4.pin2, D1.anode

notes:
  5V
  RX
  TX
  gd
  off
  (-)
  D
  D3V
  Vin
  tx
  rx
  gnd
  Ain
  scl
  3V
  sda
  Hexbotling client
  v0.4 (c) T.Euler
  0
  7
  sd
  sc

custom parts:
  Lithium Ion Polymer Battery 3.7v 350mAh: Lithium ion polymer (also known as 'lipo' or 'lipoly') batteries are thin, light and powerful. The output ranges from 4.2V when completely charged to 3.7V. This battery has a capacity of 350mAh for a total of about 1.3 Wh. The batteries come pre-attached with a genuine 2-pin JST-PH connector as shown and include the necessary protection circuitry.
