# Fritzing sketch hexpodling_v0_4 (saved by Fritzing 0.9.4)
circuit board: 7.3cm x 5.9cm
breadboards: 6

parts:
  0 = female pin header, 3 pins [form="♀ (female)"]
  R2 = Resistor [tolerance=±5% resistance=0 package=THT]
  1 = female pin header, 3 pins [form="♀ (female)"]
  R3 = Resistor [tolerance=±5% resistance=0 package=THT]
  R4 = Resistor [tolerance=±5% resistance=0 package=THT]
  2 = female pin header, 3 pins [form="♀ (female)"]
  3 = female pin header, 3 pins [form="♀ (female)"]
  0i = female pin header, 3 pins [form="♀ (female)"]
  1i = female pin header, 3 pins [form="♀ (female)"]
  2i = female pin header, 3 pins [form="♀ (female)"]
  3i = female pin header, 3 pins [form="♀ (female)"]
  4378T-3 = SOIC-14 [chip_label=SOIC-14 part_number="700-MAX4378TASD " package=SO]
  R8 = Resistor [tolerance=±5% resistance=0 package=THT]
  R6 = Resistor [tolerance=±5% resistance=0 package=THT]
  R5 = Resistor [tolerance=±5% resistance=0 package=THT]
  7i = female pin header, 3 pins [form="♀ (female)"]
  5i = female pin header, 3 pins [form="♀ (female)"]
  4i = female pin header, 3 pins [form="♀ (female)"]
  7 = female pin header, 3 pins [form="♀ (female)"]
  5 = female pin header, 3 pins [form="♀ (female)"]
  4 = female pin header, 3 pins [form="♀ (female)"]
  R12 = Resistor [tolerance=±5% resistance=12k package=THT]
  R11 = Resistor [tolerance=±5% resistance=12k package=THT]
  R10 = Resistor [tolerance=±5% resistance=12k package=THT]
  R13 = Resistor [tolerance=±5% resistance=12k package=THT]
  dummy2 = female pin header, 10 pins [form="♀ (female)"]
  dummy3 = female pin header, 10 pins [form="♀ (female)"]
  C3 = Tantalum Capacitor [capacitance=4.7µF voltage=16V package="100 mil [THT, tantalum]"]
  C4 = Tantalum Capacitor [capacitance=4.7µF voltage=16V package="100 mil [THT, tantalum]"]
  C2 = Tantalum Capacitor [capacitance=4.7µF voltage=16V package="100 mil [THT, tantalum]"]
  C1 = Tantalum Capacitor [capacitance=4.7µF voltage=16V package="100 mil [THT, tantalum]"]
  R14 = Resistor [tolerance=±5% resistance=12k package=THT]
  R15 = Resistor [tolerance=±5% resistance=12k package=THT]
  R16 = Resistor [tolerance=±5% resistance=12k package=THT]
  R17 = Resistor [tolerance=±5% resistance=12k package=THT]
  C8 = Tantalum Capacitor [capacitance=4.7µF voltage=16V package="100 mil [THT, tantalum]"]
  C7 = Tantalum Capacitor [capacitance=4.7µF voltage=16V package="100 mil [THT, tantalum]"]
  C6 = Tantalum Capacitor [capacitance=4.7µF voltage=16V package="100 mil [THT, tantalum]"]
  C5 = Tantalum Capacitor [capacitance=4.7µF voltage=16V package="100 mil [THT, tantalum]"]
  R18 = Resistor [tolerance=±5% resistance=10k package=THT]
  R19 = Resistor [tolerance=±5% resistance=22k package=THT]
  R20 = Resistor [tolerance=±5% resistance=680 package=THT]
  LED1 = LED - 3mm [color="Green (565nm)" package="3 mm [THT]"]
  4378T-2 = SOIC-14 [chip_label=SOIC-14 part_number="700-MAX4378TASD " package=SO]
  bat = female pin header, 3 pins [form="♀ (female)"]
  R1 = Resistor [tolerance=±5% resistance=0 package=THT]
  3208-1 = SO16 [chip_label=SOIC-16 part_number="579-MCP3208CISL " package=SO]
  6 = female pin header, 3 pins [form="♀ (female)"]
  R7 = Resistor [tolerance=±5% resistance=0 package=THT]
  6i = female pin header, 3 pins [form="♀ (female)"]
  Cli = female pin header, 6 pins [form="♀ (female)"]
  pot = female pin header, 3 pins [form="♀ (female)"]
  R21 = Resistor [tolerance=±5% resistance=470 package=THT]
  SC = female pin header, 7 pins [form="♀ (female)"]
  buzz = female pin header, 4 pins [form="♀ (female)"]
  R22 = Resistor [tolerance=±5% resistance=1k package=THT]
  S2 = SPST Switch [package=switch-spdt]
  LiPo_Battery_1100_mAh1 = Lithium Ion Polymer Battery 3.7v 350mAh [part_number=2750]
  LED2 = LED - 3mm [color="Red (635nm)" package="3 mm [THT]"]
  I2C = Header 4 [package=1x04-1mm-ra]
  J1 = male pin header, 2 pins [form="♂ (male)"]
  R23 = Resistor [tolerance=±5% resistance=8.2k package=THT]
  R24 = Resistor [tolerance=±5% resistance=8.2k package=THT]
  IC4 = IC, DIP package, 10 pins [chip_label=IC3 part_number=ST3002H5W]
  R25 = Resistor [tolerance=±5% resistance=220 package=THT]
  J3 = male pin header, 2 pins [form="♂ (male)"]
  LED3 = LED - 3mm [color="Red (633nm)" package="3 mm [THT]"]
  R26 = Resistor [tolerance=±5% resistance=680 package=THT]
  J2 = female pin header, 4 pins [form="♀ (female)"]
  J4 = female pin header, 3 pins [form="♀ (female)"]

nets:
  N1: 0.pin1, 1.pin1, 2.pin1, 3.pin1, 0i.pin1, 1i.pin1, 2i.pin1, 3i.pin1, 4378T-3.11, 7i.pin1, 5i.pin1, 4i.pin1, 7.pin1, 5.pin1, 4.pin1, dummy3.pin9, C3.-, C4.-, C2.-, C1.-, C8.-, C7.-, C6.-, C5.-, R18.Pin_1, R20.Pin_0, 4378T-2.11, bat.pin1, 3208-1.9, 3208-1.14, 6.pin1, 6i.pin1, Cli.pin5, pot.pin1, SC.pin1, buzz.pin3, R22.Pin_1, LiPo_Battery_1100_mAh1.negative, LED2.cathode, I2C.1, IC4.pin10, R26.Pin_0, J2.pin2, J4.pin2
  N2: 0.pin2, R2.Pin_0, 1.pin2, R3.Pin_0, R4.Pin_0, 2.pin2, 3.pin2, 4378T-3.3, 4378T-3.5, 4378T-3.10, 4378T-3.12, R8.Pin_0, R6.Pin_0, R5.Pin_0, 7.pin2, 5.pin2, 4.pin2, 4378T-2.3, 4378T-2.5, 4378T-2.10, 4378T-2.12, R1.Pin_0, 6.pin2, R7.Pin_0
  N3: 0.pin3, 0i.pin3
  N4: R2.Pin_1, 1i.pin2, 4378T-3.6
  N5: 1.pin3, 1i.pin3
  N6: R3.Pin_1, 2i.pin2, 4378T-3.9
  N7: R4.Pin_1, 3i.pin2, 4378T-3.13
  N8: 2.pin3, 2i.pin3
  N9: 3.pin3, 3i.pin3
  N10: 0i.pin2, 4378T-3.2, R1.Pin_1
  N11: 4378T-3.1, R10.Pin_1
  N12: 4378T-3.4, 4378T-2.4, 3208-1.15, 3208-1.16, Cli.pin6, SC.pin2, J2.pin1, J4.pin1
  N13: 4378T-3.7, R11.Pin_1
  N14: 4378T-3.8, R12.Pin_1
  N15: 4378T-3.14, R13.Pin_1
  N16: R8.Pin_1, 7i.pin2, 4378T-2.13
  N17: R6.Pin_1, 5i.pin2, 4378T-2.6
  N18: R5.Pin_1, 4i.pin2, 4378T-2.2
  N19: 7i.pin3, 7.pin3
  N20: 5i.pin3, 5.pin3
  N21: 4i.pin3, 4.pin3
  N22: R12.Pin_0, C2.+, 3208-1.3
  N23: R11.Pin_0, C4.+, 3208-1.2
  N24: R10.Pin_0, C3.+, 3208-1.1
  N25: R13.Pin_0, C1.+, 3208-1.4
  N26: dummy2.pin3, R18.Pin_0, R19.Pin_0
  N27: dummy2.pin4, pot.pin3
  N28: dummy2.pin5, SC.pin3
  N29: dummy2.pin6, SC.pin4
  N30: dummy2.pin7, 3208-1.10
  N31: dummy2.pin8, 3208-1.13
  N32: dummy2.pin9, 3208-1.12
  N33: dummy2.pin10, 3208-1.11
  N34: dummy3.pin1, I2C.4, R24.Pin_0
  N35: dummy3.pin2, I2C.3, J1.pin2, R23.Pin_0
  N36: dummy3.pin3, LED1.anode
  N37: dummy3.pin4, R21.Pin_1
  N38: dummy3.pin5, Cli.pin2
  N39: dummy3.pin6, Cli.pin1
  N40: dummy3.pin7, pot.pin2, I2C.2, R23.Pin_1, R24.Pin_1
  N41: dummy3.pin10, S2.P, LED3.anode, J2.pin3, J4.pin3
  N42: R14.Pin_0, C5.+, 3208-1.5
  N43: R14.Pin_1, 4378T-2.14
  N44: R15.Pin_0, C6.+, 3208-1.6
  N45: R15.Pin_1, 4378T-2.8
  N46: R16.Pin_0, C7.+, 3208-1.7
  N47: R16.Pin_1, 4378T-2.7
  N48: R17.Pin_0, C8.+, 3208-1.8
  N49: R17.Pin_1, 4378T-2.1
  N50: R19.Pin_1, bat.pin3, R25.Pin_1
  N51: R20.Pin_1, LED1.cathode
  N52: 4378T-2.9, R7.Pin_1, 6i.pin2
  N53: 6.pin3, 6i.pin3
  N54: Cli.pin4, R22.Pin_0, J1.pin1
  N55: R21.Pin_0, buzz.pin4
  N56: SC.pin6, LED2.anode
  N57: S2.S, IC4.pin7, J3.pin2
  N58: LiPo_Battery_1100_mAh1.positive, IC4.pin8, J3.pin1
  N59: IC4.pin1, R25.Pin_0
  N60: LED3.cathode, R26.Pin_1

notes:
  5V
  RX
  V+
  D
  gd
  rst
  TX2
  RX2
  Bat
  gnd
  3V3
  25
  26
  27
  15
  14
  33
  32
  bat
  |
  __
  4
  TX
  mo
  mi
  scl
  5
  hexapod v0.3
  Vi
  off
  (-)
  sda
  3V

custom parts:
  Lithium Ion Polymer Battery 3.7v 350mAh: Lithium ion polymer (also known as 'lipo' or 'lipoly') batteries are thin, light and powerful. The output ranges from 4.2V when completely charged to 3.7V. This battery has a capacity of 350mAh for a total of about 1.3 Wh. The batteries come pre-attached with a genuine 2-pin JST-PH connector as shown and include the necessary protection circuitry.
